# Fritzing sketch Project2-Analog-Blink (saved by Fritzing 0.9.3b)

parts:
  U1 = Explorer HAT Pro [part_number="Explorer HAT Pro" package=THT]
  R1 = Rotary Potentiometer (Small) [maximum_resistance=100kΩ package=THT]  # not connected

nets:
  N1: U1.5v, U1.G4, U1.H4
  N2: U1.G2, U1.H2, U1.Ground
  N3: U1.G3, U1.J3, U1.Analog_1

custom parts:
  Explorer HAT Pro: Explorer HAT Pro with 4 Output and 4 Input connections, 4 Analog Inputs and 2 bi-directional motor channels, plus power and ground.
