# Fritzing sketch Project4-Input-Output (saved by Fritzing 0.9.3b)

parts:
  U1 = Explorer HAT Pro [part_number="Explorer HAT Pro" package=THT]
  S1 = Pushbutton [package="[THT]"]
  R1 = Resistor [tolerance=±5% resistance=220 package=THT]  # not connected
  LED1 = LED - 5mm [color="Red (633nm)" package="5 mm [THT]"]  # not connected

nets:
  N1: U1.5v, U1.A12, U1.B12, U1.F5, U1.G5
  N2: U1.A13, U1.B13, U1.D13
  N3: U1.B17, U1.E17, U1.Output_1
  N4: U1.F3, U1.G3, U1.Input_1
  N5: S1.Pin_1, S1.Pin_2
  N6: S1.Pin_3, S1.Pin_4

custom parts:
  Explorer HAT Pro: Explorer HAT Pro with 4 Output and 4 Input connections, 4 Analog Inputs and 2 bi-directional motor channels, plus power and ground.
